# Fritzing sketch smart_headphone_stand with fsr (saved by Fritzing 1.0.0rc)
breadboards: 1

parts:
  Mod2 = Raspberry Pi Pico W
  R3 = Basic Force Sensing Resistor (FSR) [package=THT]
  R4 = Resistor [tolerance=±5% resistance=10k package="0805 [SMD]"]
  LED2 = LED - 5mm [color="Green (570nm)" current=0.030A package="5 mm [THT]"]
  Grove2 = Grove OLED 128x96
  LED4 = LED - 5mm [color="Red (633nm)" current=0.030A package="5 mm [THT]"]

nets:
  N1: Mod2.pin_3, Mod2.pin_8, Mod2.pin_13, Mod2.pin_18, Mod2.pin_23, Mod2.pin_28, Mod2.pin_33, Mod2.pin_38, Mod2.pin_42, R4.Pin_0, LED2.cathode, Grove2.GND, LED4.cathode
  N2: Mod2.pin_6, LED4.anode
  N3: Mod2.pin_7, LED2.anode
  N4: Mod2.pin_9, Grove2.SDA
  N5: Mod2.pin_10, Grove2.SCL
  N6: Mod2.pin_31, R3.pin_1, R4.Pin_1
  N7: Mod2.pin_36, R3.pin_2, Grove2.VCC

custom parts:
  Raspberry Pi Pico W: Raspberry Pi Pico W. Based around the RP2040 microcontroller the Pico W is a low cost microcontroller device bringing Raspberry Pi quality, cost, and easy of use to the microcontroller space. The areas marked KEEPOUT in pcb silkscreen should not have traces running through them to avoid shorts on a soldered in module!
